# Fritzing sketch esquematico (saved by Fritzing 0.9.2b)

parts:
  Componente1 = Arduino Uno (Rev3)
  GY1 = MPU-6050 Board GY-521 [form="♀ (female)" package=THT]
  GY2 = MPU-6050 Board GY-521 [form="♀ (female)" package=THT]
  LED1 = smd LED [color="Blue (430nm)" package="0603 [SMD]"]
  LED2 = smd LED [color="Red (633nm)" package="1206 [SMD]"]
  LED3 = smd LED [color="Red (633nm)" package="1206 [SMD]"]
  S1 = H-Bridge with L298N
  R3 = Resistor [tolerance=±5% resistance=220 package=THT]
  R2 = Resistor [tolerance=±5% resistance=220 package=THT]
  R1 = Resistor [tolerance=±5% resistance=220 package=THT]
  Componente2 = MAG3110
  JP1 = Header 1 [package=1x01_offset]
  JP2 = Header 1 [package=1x01_offset]

nets:
  N1: Componente1.A4/SDA, GY1.pin4, GY2.pin4, Componente2.SDA
  N2: Componente1.A5/SCL, GY1.pin3, GY2.pin3, Componente2.SCL
  N3: Componente1.D8, S1.IN1
  N4: Componente1.D9_PWM, GY2.pin8
  N5: Componente1.D10_PWM/SS, R3.Pin_1
  N6: Componente1.D11_PWM/MOSI, GY1.pin8
  N7: Componente1.D12/MISO, R2.Pin_1
  N8: Componente1.D13/SCK, R1.Pin_1
  GND: Componente1.GND, GY1.pin2, GY2.pin2, LED1.cathode, LED2.cathode, LED3.cathode, Componente2.GND
  N9: Componente1.D3_PWM, S1.IN2
  N10: Componente1.D4, S1.IN3
  N11: Componente1.D5_PWM, JP2.1
  N12: Componente1.D6_PWM, JP1.1
  N13: Componente1.D7, S1.IN4
  3V3: Componente1.3V3, Componente2.VCC
  N14: Componente1.5V, GY1.pin1, GY1.pin5, GY2.pin1
  N15: LED1.anode, R1.Pin_0
  N16: LED2.anode, R2.Pin_0
  N17: LED3.anode, R3.Pin_0

notes:
  Elevación
  Azimituh
  ENB, ENA

custom parts:
  MPU-6050 Board GY-521: Acelerometro y Giroscopio MPU-6050 Board GY-521
  H-Bridge with L298N: h-bridge
  MAG3110: Sparkfun MAG3110 Breakout
