# Fritzing sketch pcb2 (saved by Fritzing 0.9.2b)
circuit board: 2.11478cm x 2.05217cm
circuit board: 3.56878cm x 3.91346cm
circuit board: 2.58449cm x 2.52188cm

parts:
  GY5 = MPU-6050 Board GY-521 [form="♀ (female)" package=THT]
  Part3 = Triple Axis Magnetometer - HMC5883 Breakout
  JP14 = Header 3 [package=molex-1x3_lock]
  GY6 = MPU-6050 Board GY-521 [form="♀ (female)" package=THT]
  GY7 = MPU-6050 Board GY-521 [form="♀ (female)" package=THT]
  R1 = Resistor [tolerance=±5% resistance=220 package=THT]
  R2 = Resistor [tolerance=±5% resistance=220 package=THT]
  R3 = Resistor [tolerance=±5% resistance=220 package=THT]
  LED6 = LED - 3mm [color="Red (633nm)" package="3 mm [THT]"]
  LED7 = LED - 3mm [color="Red (633nm)" package="3 mm [THT]"]
  LED5 = LED - 3mm [color="Red (633nm)" package="3 mm [THT]"]
  GY8 = MPU-6050 Board GY-521 [form="♀ (female)" package=THT]
  GY9 = MPU-6050 Board GY-521 [form="♀ (female)" package=THT]
  JP15 = Header 5x2 [package=2x5-raf]

nets:
  N1: GY5.pin1, GY6.pin1, GY7.pin1
  N2: GY5.pin5, Part3.SDA, GY6.pin5, GY7.pin5
  N3: GY5.pin6, Part3.SCL, GY6.pin6, GY7.pin6, LED6.cathode, LED7.cathode, LED5.cathode
  N4: GY5.pin7, Part3.GND, GY6.pin7, GY7.pin7
  N5: GY5.pin8, Part3.VCC, GY6.pin8, GY7.pin8
  N6: JP14.1, R2.Pin_0
  N7: JP14.2, R3.Pin_1
  N8: JP14.3, R1.Pin_1
  N9: R1.Pin_0, LED7.anode
  N10: R2.Pin_1, LED5.anode
  N11: R3.Pin_0, LED6.anode
  N12: GY8.pin1, GY9.pin1
  N13: GY8.pin5, GY9.pin2, GY9.pin5
  N14: GY8.pin6, GY9.pin6
  N15: GY8.pin7, GY9.pin7
  N16: GY8.pin8, GY9.pin8
  N17: JP15.1, JP15.2
  N18: JP15.3, JP15.4
  N19: JP15.5, JP15.6
  N20: JP15.7, JP15.8
  N21: JP15.9, JP15.10

notes:
  Azimuth

custom parts:
  MPU-6050 Board GY-521: Acelerometro y Giroscopio MPU-6050 Board GY-521
